# Fritzing sketch luz_mic (saved by Fritzing 0.9.3b)
breadboards: 1

parts:
  IC1 = DIP - 8 pins [part_number=LM741 package="DIP (Dual Inline) [THT]"]
  IC2 = DIP - 8 pins [part_number=LM741 package="DIP (Dual Inline) [THT]"]
  U2 = POT [package=pot_alpha_rv16af-20]
  U3 = POT [package=pot_alpha_rv16af-20]
  C1 = Electrolytic Capacitor [capacitance=100µF voltage=35V package="200 mil [THT, electrolytic]"]
  Componente2 = Adafruit MAX4466 Electret Microphone Amplifier [part_number="Adafruit #1063"]
  R1 = Resistor [tolerance=±5% resistance=1M package=THT]
  R2 = Resistor [tolerance=±5% resistance=1M package=THT]
  R3 = Resistor [tolerance=±5% resistance=100 package=THT]
  LED1 = LED - 5mm [color="Yellow (585nm)" package="5 mm [THT]"]
  R4 = Resistor [tolerance=±5% resistance=1k package=THT]
  VCC1 = Battery block 9V

nets:
  N1: IC1.pin2, U2.E, R3.Pin_0
  N2: IC1.pin3, Componente2.OUT, R1.Pin_0, R2.Pin_0
  N3: IC1.pin4, IC2.pin4, U3.A, C1.-, Componente2.GND, R2.Pin_1, R4.Pin_0, VCC1.-
  N4: IC1.pin6, IC2.pin2, U2.S
  N5: IC1.pin7, IC2.pin7, U3.E, Componente2.VCC, R1.Pin_1, VCC1.+
  N6: IC2.pin3, U3.S
  N7: IC2.pin6, LED1.anode
  N8: C1.+, R3.Pin_1
  N9: LED1.cathode, R4.Pin_1

notes:
  Projeto com microfone com LED, de Ernesto Flôres Barreira (9/6/2018)

custom parts:
  DIP - 8 pins: A DIP stand-in part for whatever IC you want. With 8 pins on a 300 mil dual inline package (DIP) footprint.
  Adafruit MAX4466 Electret Microphone Amplifier: Add an ear to your project with this well-designed electret microphone amplifier. This fully assembled and tested board comes with a 20-20KHz electret microphone soldered on. For the amplification, we use the Maxim MAX4466, an op-amp specifically designed for this delicate task! The amplifier has excellent power supply noise rejection, so this amplifier sounds really good and isn't nearly as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
